# Fritzing sketch diagrama (saved by Fritzing 0.9.3b)
breadboards: 2

parts:
  U2 = NodeMCU V3.0 [part_number="Lolin v0.1"]
  L298N1 = L298N DC motor driver
  M1 = DC Motor  # not connected
  Power_plug1 = Power plug
  M2 = DC Motor  # not connected
  hc-sr1 = hc-sr04
  Keyes1 = Keyes IR Infrared Sensor Switch Module
  Keyes2 = Keyes IR Infrared Sensor Switch Module

nets:
  N1: U2.D1, hc-sr1.Echo
  N2: U2.D2, hc-sr1.Trig
  N3: U2.D3, Keyes1.out
  N4: U2.D4, Keyes2.out
  3V3: U2.3V3, L298N1.5V
  GND: U2.GND#6, U2.GND#13, U2.GND#16, U2.GND#33, L298N1.GND, Power_plug1.GND
  N5: U2.D5, L298N1.IN2
  N6: U2.D6, L298N1.IN1
  N7: U2.D7, L298N1.IN3
  N8: U2.D8, L298N1.IN4
  12V: L298N1.12V, Power_plug1.VCC
  VCC: hc-sr1.VCC, Keyes1.VCC, Keyes2.VCC
  GND_2: hc-sr1.GND, Keyes1.GND, Keyes2.GND

custom parts:
  NodeMCU V3.0: ESP8266 based NodeMCU
  L298N DC motor driver: 2x DC motor driver with 78M05 positive voltage regulator (7..35 V) L298N: max 46 V, 2 A Set 5 V Enable jumper to enable 5 V regultor (needed for the L298N) and +5 V output at screw terminal or supply external +5 V at screw terminal Set ENA and/or ENB to +5 V to enable motor permanently or supply ENA and/or ENB with PWM signal IN1 and IN2 set rotation directory for motor A (OUT1/OUT2) IN2 and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
  Keyes IR Infrared Sensor Switch Module: An infrared obstacle detector
